// Logisim project rgb_driver.circ as structural Verilog: 1 circuit, main circuit main
module main (
);

  wire and_1_out, and_2_out, and_3_out, and_4_out, and_5_out, and_6_out, and_7_out, and_8_out, and_9_out,
       and_10_out, and_11_out, clock_1_out, comparator_1_eq, comparator_2_eq, d_ff_1_q, d_ff_2_q, d_ff_3_q,
       d_ff_3_qn, j_k_ff_1_q, j_k_ff_1_qn, nand_1_out, nor_1_out, not_1_out, not_2_out, not_3_out, or_1_out,
       or_2_out;
  wire [3:0] counter_3_q;
  wire [7:0] counter_1_q;
  wire [15:0] counter_4_q, decoder_1_out0, ram_1_data, register_1_q;
  wire [16:0] counter_2_q;

  Clock clock_1 (.out(clock_1_out));
  Counter counter_1 (.count(and_1_out), .Q(counter_1_q), .clk(clock_1_out), .clr(and_2_out));  // open: load, D, carry
  Counter #(.width(17), .max('h1ffff)) counter_2 (
    .count(or_1_out), .Q(counter_2_q), .clk(clock_1_out), .clr(and_2_out));  // open: load, D, carry
  // Probe on counter_1_q
  and and_1 (and_1_out, ram_1_data[13], and_5_out);
  and and_2 (and_2_out, ram_1_data[14], and_5_out);
  or or_1 (or_1_out, not_1_out, and_5_out);
  not not_1 (not_1_out, ram_1_data[12]);
  and and_3 (and_3_out, register_1_q[13], and_5_out);
  RAM #(.addrWidth(17), .dataWidth(16), .bus("asynch")) ram_1 (
    .addr(counter_2_q), .data(ram_1_data));  // open: sel, ld, clr
  not not_2 (not_2_out, register_1_q[13]);
  and and_4 (and_4_out, register_1_q[12], not_2_out, and_5_out);
  Counter #(.width(4), .max('hf)) counter_3 (
    .load(and_3_out), .D(4'b0010), .count(and_4_out), .Q(counter_3_q), .clk(clock_1_out));  // open: carry, clr
  Register #(.width(16)) register_1 (.D(ram_1_data), .Q(register_1_q), .clk(clock_1_out));  // open: en, clr
  and and_5 (and_5_out, and_6_out, j_k_ff_1_q, d_ff_3_q);
  D_Flip_Flop d_ff_1 (.clk(clock_1_out), .D(register_1_q[12]), .Q(d_ff_1_q));  // open: Qn, preset, en, reset
  nand nand_1 (nand_1_out, j_k_ff_1_q, d_ff_3_q);
  Decoder #(.select(4)) decoder_1 (
    .out0(decoder_1_out0[0]), .out1(decoder_1_out0[1]), .out2(decoder_1_out0[2]), .out3(decoder_1_out0[3]),
    .out4(decoder_1_out0[4]), .out5(decoder_1_out0[5]), .out6(decoder_1_out0[6]), .out7(decoder_1_out0[7]),
    .out8(decoder_1_out0[8]), .out9(decoder_1_out0[9]), .out10(decoder_1_out0[10]),
    .out11(decoder_1_out0[11]), .out12(decoder_1_out0[12]), .out13(decoder_1_out0[13]),
    .out14(decoder_1_out0[14]), .out15(decoder_1_out0[15]), .sel(counter_3_q));  // open: en
  and and_6 (and_6_out, register_1_q[12], d_ff_1_q);
  and and_7 (and_7_out, and_6_out, nand_1_out);
  nor nor_1 (nor_1_out, and_6_out, clock_1_out);
  not not_3 (not_3_out, and_6_out);
  Counter #(.width(16), .max('hffff)) counter_4 (
    .count(and_7_out), .Q(counter_4_q), .clk(clock_1_out), .clr(or_2_out));  // open: load, D, carry
  or or_2 (or_2_out, not_3_out, and_8_out);
  Shift_Register #(.length(32)) shift_register_1 (
    .in(register_1_q[0]), .clk(nor_1_out));  // open: shift, out, load, clr, d0, q0, d1, q1, d2, q2, d3, q3, d4, q4, d5, q5, d6, q6, d7, q7, d8, q8, d9, q9, d10, q10, d11, q11, d12, q12, d13, q13, d14, q14, d15, q15, d16, q16, d17, q17, d18, q18, d19, q19, d20, q20, d21, q21, d22, q22, d23, q23, d24, q24, d25, q25, d26, q26, d27, q27, d28, q28, d29, q29, d30, q30, d31, q31
  Shift_Register #(.length(32)) shift_register_2 (
    .in(register_1_q[1]), .clk(nor_1_out));  // open: shift, out, load, clr, d0, q0, d1, q1, d2, q2, d3, q3, d4, q4, d5, q5, d6, q6, d7, q7, d8, q8, d9, q9, d10, q10, d11, q11, d12, q12, d13, q13, d14, q14, d15, q15, d16, q16, d17, q17, d18, q18, d19, q19, d20, q20, d21, q21, d22, q22, d23, q23, d24, q24, d25, q25, d26, q26, d27, q27, d28, q28, d29, q29, d30, q30, d31, q31
  Shift_Register #(.length(32)) shift_register_3 (
    .in(register_1_q[2]), .clk(nor_1_out));  // open: shift, out, load, clr, d0, q0, d1, q1, d2, q2, d3, q3, d4, q4, d5, q5, d6, q6, d7, q7, d8, q8, d9, q9, d10, q10, d11, q11, d12, q12, d13, q13, d14, q14, d15, q15, d16, q16, d17, q17, d18, q18, d19, q19, d20, q20, d21, q21, d22, q22, d23, q23, d24, q24, d25, q25, d26, q26, d27, q27, d28, q28, d29, q29, d30, q30, d31, q31
  Shift_Register #(.length(32)) shift_register_4 (
    .in(register_1_q[3]), .clk(nor_1_out));  // open: shift, out, load, clr, d0, q0, d1, q1, d2, q2, d3, q3, d4, q4, d5, q5, d6, q6, d7, q7, d8, q8, d9, q9, d10, q10, d11, q11, d12, q12, d13, q13, d14, q14, d15, q15, d16, q16, d17, q17, d18, q18, d19, q19, d20, q20, d21, q21, d22, q22, d23, q23, d24, q24, d25, q25, d26, q26, d27, q27, d28, q28, d29, q29, d30, q30, d31, q31
  // Probe on nor_1_out
  J_K_Flip_Flop j_k_ff_1 (
    .J(counter_4_q[2]), .clk(clock_1_out), .K(not_3_out), .Q(j_k_ff_1_q), .Qn(j_k_ff_1_qn));  // open: preset, en, reset
  D_Flip_Flop d_ff_2 (.clk(clock_1_out), .D(j_k_ff_1_qn), .Q(d_ff_2_q));  // open: Qn, preset, en, reset
  and and_8 (and_8_out, j_k_ff_1_q, d_ff_2_q);
  // Probe on counter_4_q
  Comparator comparator_1 (.a(counter_4_q[15:8]), .b(decoder_1_out0[15:8]), .eq(comparator_1_eq));  // open: gt, lt
  Comparator comparator_2 (.a(counter_4_q[7:0]), .b(decoder_1_out0[7:0]), .eq(comparator_2_eq));  // open: gt, lt
  // Probe on and_9_out
  and and_9 (and_9_out, and_6_out, j_k_ff_1_q, d_ff_3_qn);
  // Probe on and_10_out
  and and_10 (and_10_out, and_6_out, j_k_ff_1_qn);
  and and_11 (and_11_out, comparator_1_eq, comparator_2_eq);
  D_Flip_Flop d_ff_3 (.clk(clock_1_out), .D(and_11_out), .Q(d_ff_3_q), .Qn(d_ff_3_qn));  // open: preset, en, reset
endmodule
